# Fritzing sketch schema_moduleA (saved by Fritzing 0.8.5b)
breadboards: 1

parts:
  R1 = Resistor [tolerance=±5% resistance=200 package=THT]
  LED1 = LED - 5mm [color="Yellow (585nm)" package="5 mm [THT]"]
  R2 = Resistor [tolerance=±5% resistance=220 package=THT]
  LED2 = LED - 5mm [color="Green (555nm)" package="5 mm [THT]"]
  S1 = Pushbutton [package="[THT]"]
  Part1 = Arduino Pro
  X1 = USB Connectors [package=usb-minib-old]
  U3 = RFM22 [package=rfm22-xxx-s2]

nets:
  N1: R1.Pin_0, LED1.anode
  GND: R1.Pin_1, R2.Pin_1, Part1.GND, X1.GND, U3.GPIO0
  N2: LED1.cathode, S1.Pin_1, S1.Pin_2, Part1.D12/MISO
  N3: R2.Pin_0, LED2.cathode
  N4: LED2.anode, Part1.D13/SCK
  3V3: S1.Pin_3, S1.Pin_4, Part1.3V3, U3.VCC
  N5: Part1.D1/TX, U3.GPIO1
  N6: Part1.D0/RX, U3.GPIO2
  N7: Part1.5V, X1.VBUS
