# Fritzing sketch schema_moduleB (saved by Fritzing 0.8.5b)
breadboards: 1

parts:
  Raspberry_Pi_B_rev1 = Raspberry Pi B rev1
  S1 = Pushbutton [package="[THT]"]
  R1 = Resistor [tolerance=±5% resistance=200 package=THT]
  LED1 = LED - 5mm [color="Yellow (585nm)" package="5 mm [THT]"]
  LED2 = LED - 5mm [color="Green (555nm)" package="5 mm [THT]"]  # not connected
  R2 = Resistor [tolerance=±5% resistance=200 package=THT]
  R3 = Resistor [tolerance=±5% resistance=220 package=THT]
  LED3 = LED - 5mm [color="Red (633nm)" package="5 mm [THT]"]  # not connected

nets:
  N1: Raspberry_Pi_B_rev1.3V3, S1.Pin_3, S1.Pin_4
  N2: Raspberry_Pi_B_rev1.GPIO_22, S1.Pin_1, S1.Pin_2, LED1.anode
  N3: Raspberry_Pi_B_rev1.GND, R1.Pin_1, R2.Pin_1, R3.Pin_1
  N4: R1.Pin_0, LED1.cathode
