# Fritzing sketch schema_moduleA (saved by Fritzing 0.8.5b)
breadboards: 1

parts:
  R1 = Resistor [tolerance=±5% resistance=200 package=THT]
  LED1 = LED - 5mm [color="Yellow (585nm)" package="5 mm [THT]"]
  R2 = Resistor [tolerance=±5% resistance=220 package=THT]
  LED2 = LED - 5mm [color="Green (555nm)" package="5 mm [THT]"]
  S1 = Pushbutton [package="[THT]"]
  Part1 = Arduino Pro
  µUSB = IC, DIP package, 4 pins [chip_label=uUSB]
  R3 = Resistor [tolerance=±5% resistance=330 package=THT]
  R4 = Resistor [tolerance=±5% resistance=330 package=THT]
  R6 = Resistor [tolerance=±5% resistance=330 package=THT]
  HC-12 = IC, DIP package, 6 pins [chip_label=HC-12]
  L1 = Inductor [package="400 mil [THT]"]
  R7 = Resistor [tolerance=±5% resistance=330 package=THT]

nets (from the schematic view):
  N1: R1.Pin_0, LED1.cathode
  N2: R1.Pin_1, R2.Pin_1, Part1.GND, µUSB.pin2, R3.Pin_1, R4.Pin_1, R6.Pin_1, HC-12.pin5, R7.Pin_1
  N3: LED1.anode, S1.Pin_3, S1.Pin_4, Part1.D2
  N4: R2.Pin_0, LED2.cathode
  N5: LED2.anode, Part1.D7
  N6: S1.Pin_1, S1.Pin_2, Part1.5V, µUSB.pin1, R3.Pin_0, R4.Pin_0, R6.Pin_0, HC-12.pin6, R7.Pin_0
  N7: Part1.D1/TX, HC-12.pin2
  N8: Part1.D0/RX, HC-12.pin1
  N9: HC-12.pin4, L1.pin_0
