# Fritzing sketch schema_moduleB (saved by Fritzing 0.8.5b)
breadboards: 1

parts:
  S1 = Pushbutton [package="[THT]"]
  LED2 = LED - 5mm [color="Green (555nm)" package="5 mm [THT]"]
  R2 = Resistor [tolerance=±5% resistance=200 package=THT]
  R3 = Resistor [tolerance=±5% resistance=200 package=THT]
  Part1 = Arduino Pro
  RELAY = Relay [part_number=FRS1B-S package=THT]
  HC-12 = IC, DIP package, 6 pins [chip_label=HC-12]
  µUSB = IC, DIP package, 4 pins [chip_label=uUSB]
  R8 = Resistor [tolerance=±5% resistance=330 package=THT]
  R9 = Resistor [tolerance=±5% resistance=330 package=THT]
  R10 = Resistor [tolerance=±5% resistance=330 package=THT]
  R11 = Resistor [tolerance=±5% resistance=330 package=THT]
  LED3 = LED - 3mm [color="Red (633nm)" package="3 mm [THT]"]
  L1 = Inductor [package="400 mil [THT]"]

nets (from the schematic view):
  N1: S1.Pin_1, S1.Pin_2, R2.Pin_1, R3.Pin_1, Part1.GND, RELAY.COIL2, HC-12.pin5, µUSB.pin2, R8.Pin_1, R9.Pin_1, R10.Pin_1, R11.Pin_1
  N2: S1.Pin_3, S1.Pin_4, Part1.RESET
  N3: LED2.cathode, R3.Pin_0
  N4: LED2.anode, Part1.D6_PWM
  N5: R2.Pin_0, LED3.cathode
  N6: Part1.D0/RX, HC-12.pin1
  N7: Part1.D5_PWM, RELAY.COIL1
  N8: Part1.D7, LED3.anode
  N9: Part1.5V, HC-12.pin6, µUSB.pin1, R8.Pin_0, R9.Pin_0, R10.Pin_0, R11.Pin_0
  N10: HC-12.pin4, L1.pin_0
